# Fritzing sketch SchemaCircuitPillGiver (2) (saved by Fritzing 0.9.6b)
breadboards: 1

parts:
  Mod1 = Raspberry Pi 4B
  Driver1 = 28BYJ-48 Driver Module [part_number=ULN2003 package=THT]
  SM1 = 28BYJ-48 Stepper Motor [part_number=28BYJ-48]
  C1 = Electrolytic Capacitor [capacitance=1μF voltage=35V package="0405 [SMD, electrolytic]"]
  R1 = Photocell (LDR) [package=THT]
  active_buzzer1 = Active buzzer [package=THT]
  M1 = fc-51 [package=THT]
  S1 = Momentary Switch [package=ksa_sealed_tac_switch]
  S2 = Momentary Switch [package=ksa_sealed_tac_switch]
  C2 = Electrolytic Capacitor [capacitance=1μF voltage=35V package="0405 [SMD, electrolytic]"]
  C3 = Electrolytic Capacitor [capacitance=1μF voltage=35V package="0405 [SMD, electrolytic]"]
  LED1 = RGB LED (com. cathode, rgb) [color="Red (633nm)" current=0.030A package="5 mm [THT]"]
  R2 = Resistor [tolerance=±5% resistance=220 package="0805 [SMD]"]
  R3 = Resistor [tolerance=±5% resistance=220 package="0805 [SMD]"]
  R5 = Resistor [tolerance=±5% resistance=220 package="0805 [SMD]"]

nets:
  N1: Mod1.3V3, R1.pin_0, M1.pin3, S1.3, S2.3
  N2: Mod1.5V, Driver1.Vmotor
  N3: Mod1.GPIO4, M1.pin1
  GND: Mod1.GND, Mod1.GPIO13, Driver1.IN2, Driver1.GND, C1.-, active_buzzer1.GND, M1.pin2, C2.-, C3.-, LED1.common_cathode
  N4: Mod1.GPIO17, S1.1, C3.+
  N5: Mod1.GPIO18, active_buzzer1.Vcc
  N6: Mod1.GPIO27, S2.1, C2.+
  N7: Mod1.GPIO7, C1.+, R1.pin_1
  N8: Mod1.GPIO6, Mod1.GPIO12, Driver1.IN1
  N9: Mod1.GPIO19, Mod1.GPIO16, Driver1.IN3, LED1.red_anode, R5.Pin_0, R5.Pin_1
  N10: Mod1.GPIO26, Driver1.IN4
  N11: Mod1.GPIO20, LED1.green_anode, R3.Pin_0, R3.Pin_1
  N12: Mod1.GPIO21, LED1.blue_anode, R2.Pin_0, R2.Pin_1
  N13: Driver1.blue-pin, SM1.blue-pin
  N14: Driver1.pink-pin, SM1.pink-pin
  N15: Driver1.yellow-pin, SM1.yellow-pin
  N16: Driver1.orange-pin, SM1.orange-pin
  N17: Driver1.red-pin, SM1.red-pin

notes:
  KETERANGAN KABEL:
  Orange: Power/VCC 3v3
  Red: Power/VCC 5v
  Back: Ground/GND
  pin VCC 5v kedua dan ground yg disebelahnya tdk dipakai karena ada lobang kipas
  TECHNICAL NOTES: (BUKAN BUAT DINILAI) (lagian penataan katanya jelek disini)
  Untuk penilaian di bawah sini saja :D
  SPI jangan dinyalain. Awas ntar motornya dikira chip :/
  Untuk tombol kanan: menyalakan voice command (semacam Google Assistant, tetapi tidak menekan tombol home),
  Untuk tombol kiri: menyalakan motornya tanpa harus menyalakan voice command ataupun sensor
  Mengapa saya lebih suka memakai Capacitor untuk tombol tersebut?
  Supaya arus tersebut bisa direkam oleh mesin tersebut (Raspberry Pi) dengan cara menyimpan daya secara cepat setelah arus listrik mengalir saat tombol ditekan
  3 Kaki LED tersebut (RGB LED) hanya menyala jika mode tersebut diaktifkan (Voice Command, Speaking, dsb)
  LDR ini hanya mendeksi jika ada cahaya, motor jalan
  Buzzer ini hanya berbunyi jika mode tertentu selesai dijalankan
  Kalau sudah selesai boleh memasukkan speaker ke dalam lubang aux maupun usb.
  Sayangnya lubang aux yang ada di Raspberry Pi tersebut tidak ada untuk input, jadi untuk microphone boleh dimasukkan ke dalam usb ataupun secara bluetooth
  Infrared ini hanya mendeteksi jika ada benda, motor berjalan
  Motor ini bergerak secara berputar di pintu vending machine tersebut

custom parts:
  28BYJ-48 Driver Module: ULN2003 Driver Module for the 28BYJ-48 Unipolar Stepper Motor LED A - Blue wire - Bottom coil left LED B - Pink wire - Top coil left LED C - Yellow wire - Bottom coil right LED D - Orange wire - Top coil right Common rail - red Connector pins: blue - pink - yellow - orange - red Control pins - IN1 to IN4 Power pins - GND & Vmotor (5-12V) On/Off jumper (if removed, power to motor is cut).
  28BYJ-48 Stepper Motor: Unipolar Stepper Motor 28BYJ-48 Top coil - pink & orange Bottom coil - blue & yellow Common rail - red Connector pins: blue - pink - yellow - orange - red
  Active buzzer: Active buzzer 12 mm, 3-5 V
